// Digital circuit mode_selector.dig as structural Verilog
module mode_selector (
  input  ID,
  input  PWD,
  input  DIS,
  input  RESET,
  input  CLK,
  input  RST,
  output IDO,
  output PWDO
);

  mode_selector #(.applicationType("IVERILOG")) u_mode_selector (
    .clk(CLK), .reset(RST), .ID(ID), .PWD(PWD), .DIS(DIS), .timer_reset(RESET), .PWDO(PWDO), .IDO(IDO));
endmodule

/* Code of mode_selector:
module mode_selector (
  input wire clk,         // Clock signal
  input wire reset,       // Classic reset signal
  input wire ID,          // ID button
  input wire PWD,         // PASSWORD button
  input wire DIS,         // Timer output signal
  input wire timer_reset, // Reset signal from timer circuit
  output wire PWDO,       // Password output
  output wire IDO         // ID output
);

  reg [1:0] mode_reg;     // Register to store the current mode
  reg [1:0] prev_mode;    // Register to store the previous mode
  reg DIS_prev;           // Register to store the previous DIS signal
  reg deasserted;         // Flag to track DIS deassertion

  always @(posedge clk or posedge reset or posedge timer_reset) begin
    if (~reset) begin
      mode_reg <= 2'b01;       // Reset the mode to initial state (ID mode)
      DIS_prev <= 1'b0;        // Reset the previous DIS signal
      deasserted <= 0;         // Reset the deasserted flag
    end else begin
      // Mode transition logic based on button inputs and DIS signal
      if (ID) begin
        prev_mode <= mode_reg; // Store the previous mode
        mode_reg <= 2'b01;     // Switch to ID mode when ID is asserted
        deasserted <= 0;       // Reset the deasserted flag
      end else if (PWD) begin
        prev_mode <= mode_reg; // Store the previous mode
        mode_reg <= 2'b10;     // Switch to PASSWORD mode when PWD is asserted
        deasserted <= 0;       // Reset the deasserted flag
      end else if (DIS && ~DIS_prev && (mode_reg == 2'b10)) begin
        prev_mode <= mode_reg; // Store the previous mode
        deasserted <= 1;       // Set the deasserted flag
      end else if (~DIS && (mode_reg == 2'b10) && deasserted) begin
        prev_mode <= mode_reg; // Store the previous mode
        mode_reg <= 2'b01;     // Switch to ID mode when DIS is deasserted after being asserted
        deasserted <= 0;       // Reset the deasserted flag
      end else if (DIS && (mode_reg == 2'b01)) begin
        prev_mode <= mode_reg; // Store the previous mode
        deasserted <= 0;       // Reset the deasserted flag
      end else if (timer_reset) begin
        mode_reg <= 2'b01;     // Reset to ID mode when timer is reset
        deasserted <= 0;       // Reset the deasserted flag
      end

      DIS_prev <= DIS;         // Update the previous DIS signal
    end
  end

  // Output logic based on the current mode
  assign PWDO = (mode_reg == 2'b10) ? 1'b1 : 1'b0;
  assign IDO = (mode_reg == 2'b01) ? 1'b1 : 1'b0;

endmodule
*/
