// Digital circuit shifter.dig as structural Verilog
module shifter (
  input  [3:0] IN,
  input  EN,
  input  DA,
  input  CLK,
  input  RST,
  output [3:0] ID1,
  output [3:0] ID0,
  output [7:0] HEX
);

  wire and_1_out;
  wire [7:0] mul_1_mul;

  and and_1 (and_1_out, EN, DA, RST);
  D_FF #(.Bits(4)) d_ff_1 (.D(IN), .C(and_1_out), .Q(ID0));  // open: nQ
  Seven_Seg_Hex seven_seg_hex_1 (.d(ID1), .dp(1'b0));
  D_FF #(.Bits(4)) d_ff_2 (.D(ID0), .C(and_1_out), .Q(ID1));  // open: nQ
  Seven_Seg_Hex seven_seg_hex_2 (.d(ID0), .dp(1'b0));
  Mul #(.Bits(4)) mul_1 (.a(ID1), .b(4'b1010), .mul(mul_1_mul));
  Seven_Seg_Hex seven_seg_hex_3 (.d(4'b1010), .dp(1'b0));
  Add #(.Bits(8)) add_1 (.a({4'b0000, ID0}), .b(mul_1_mul), .c_i(1'b0), .s(HEX));  // open: c_o
endmodule
