// Digital circuit shifter_pwd.dig as structural Verilog
module shifter_pwd (
  input  [3:0] DATA_in,
  input  [15:0] PWD_in,
  input  EN,
  input  DA,
  input  CLK,
  input  RST,
  output MATCH,
  output LED1,
  output LED2,
  output LED3,
  output LED4
);

  shifter_pwd #(.applicationType("IVERILOG")) u_shifter_pwd (
    .clk(CLK), .rst(RST), .DATA(DATA_in), .PWD(PWD_in), .EN(EN), .DA(DA), .MATCH(MATCH), .LED1(LED1),
    .LED2(LED2), .LED3(LED3), .LED4(LED4));
endmodule

/* Code of shifter_pwd:
module shifter_pwd (
  input wire clk,            // Clock signal
  input wire rst,            // Reset signal
  input wire [3:0] DATA,     // Input from encoder (4 bits)
  input wire [15:0] PWD,     // Password from ROM (16 bits BCD)
  input wire EN,             // Mode selector output (PWDO)
  input wire DA,             // Input from encoder
  output wire MATCH,         // Output for granting access (LED "granted")
  output wire LED1,          // Output for first digit LED
  output wire LED2,          // Output for second digit LED
  output wire LED3,          // Output for third digit LED
  output wire LED4           // Output for fourth digit LED
);

  reg [15:0] entered_code;   // Entered code from keypad
  reg [3:0] digit_count;     // Counter for number of entered digits
  reg match;                 // Flag for code match

  always @(posedge clk or posedge rst) begin
    if (~rst || ~EN) begin
      entered_code <= 16'b0; // Reset entered code
      digit_count <= 4'b0;   // Reset digit count
      match <= 1'b0;         // Reset match flag
    end else begin
      if (EN) begin
        if (DA) begin
          // Handle shifting and storing of entered code
          if (digit_count < 4) begin
            entered_code <= {entered_code[11:0], DATA};
            digit_count <= digit_count + 1;
          end
        end
      end
    end
  end

  // Output logic for LED display
  assign LED1 = (digit_count >= 1);
  assign LED2 = (digit_count >= 2);
  assign LED3 = (digit_count >= 3);
  assign LED4 = (digit_count >= 4);

  // Output logic for code matching
  always @* begin
    if (digit_count == 4) begin
      if (entered_code == PWD)
        match = 1'b1;
      else
        match = 1'b0;
    end else begin
      match = 1'b0;
    end
  end

  // Output logic for granting access
  assign MATCH = match;

endmodule
*/
